// Logisim project risc_v_cpu.circ as structural Verilog: 6 circuits, main circuit main
module main (
  input  reset,
  output [31:0] current_pc,
  output [31:0] current_instruction,
  output [31:0] alu_output,
  output [31:0] dmem_output,
  output [31:0] rd_write_value,
  output [31:0] data_rs1,
  output [31:0] data_rs2,
  output [31:0] imm_32bit,
  output [3:0] alu_select,
  output imm_vs_rs2_select,
  output enable_rd_write,
  output [2:0] imm_type,
  output jump_branch,
  output [1:0] rd_write_select,
  output next_pc_select,
  output dmem_write_enable,
  output halt
);

  wire clk, eq, gt, lt;
  wire [31:0] multiplexer_1_out, multiplexer_2_out, multiplexer_3_out, PCplus4;

  Clock clock_1 (.out(clk));
  Multiplexer #(.width(32)) multiplexer_1 (
    .in0(PCplus4), .in1(alu_output), .out(multiplexer_1_out), .sel(next_pc_select));
  Register #(.width(32)) PC (.D(multiplexer_1_out), .en(1'b1), .clk(clk), .Q(current_pc), .clr(reset));
  Adder #(.width(32)) adder_1 (.a(32'h4), .b(current_pc), .out(PCplus4));  // open: cin, cout
  ROM #(.addrWidth(24), .dataWidth(32)) imem (.addr(current_pc[25:2]), .data(current_instruction));
  better_control better_control_1 (
    .instruction(current_instruction), .eq(eq), .lt(lt), .alu_select(alu_select),
    .get_immediate(imm_vs_rs2_select), .enable_rd_write(enable_rd_write), .Imm_type(imm_type),
    .jump(jump_branch), .select_rd_write(rd_write_select), .next_pc_select(next_pc_select),
    .dmem_write_enable(dmem_write_enable));
  regfile regfile_1 (
    .input_data(rd_write_value), .address_rd(current_instruction[11:7]),
    .address_rs1(current_instruction[19:15]), .address_rs2(current_instruction[24:20]),
    .write_enable(enable_rd_write), .clk(clk), .reset(reset), .data_rs1(data_rs1), .data_rs2(data_rs2));
  get_immediate_value get_immediate_value_1 (
    .instruction(current_instruction), .Imm_type(imm_type), .Immediate(imm_32bit));
  Comparator #(.width(32)) comparator_1 (.a(data_rs1), .b(data_rs2), .gt(gt), .eq(eq), .lt(lt));
  Multiplexer #(.width(32)) multiplexer_2 (
    .in0(data_rs1), .in1(current_pc), .out(multiplexer_2_out), .sel(jump_branch));
  Multiplexer #(.width(32)) multiplexer_3 (
    .in0(data_rs2), .in1(imm_32bit), .out(multiplexer_3_out), .sel(imm_vs_rs2_select));
  Comparator #(.width(32)) comparator_2 (.a(current_instruction), .b(32'h6f), .eq(halt));  // open: gt, lt
  alu alu_1 (.rs1(multiplexer_2_out), .rs2(multiplexer_3_out), .alu_select(alu_select), .rd(alu_output));
  RAM #(.addrWidth(24), .clearpin("true"), .dataWidth(32), .enables("line")) dmem (
    .addr(alu_output[25:2]), .we(dmem_write_enable), .clk(clk), .din(data_rs2), .dout(dmem_output),
    .clr(reset));
  Multiplexer #(.select(2), .width(32)) multiplexer_4 (
    .in0(dmem_output), .in1(alu_output), .in2(PCplus4), .out(rd_write_value), .sel(rd_write_select));  // open: in3

  // Other names for the same wires on the sheet: dmemory_write_enable = dmem_write_enable;
  //   immediate[31:0] = imm_32bit; instruction[31:0] = current_instruction; opcode[6:0] = current_instruction[6:0];
  //   rd[4:0] = current_instruction[11:7]; func3[2:0] = current_instruction[14:12];
  //   rs1[4:0] = current_instruction[19:15]; rs2[4:0] = current_instruction[24:20];
  //   func7[6:0] = current_instruction[31:25]; jump = jump_branch

  // Notes on the sheet:
  //   CLOCK
  //   INSTRUCTION FETCH
  //   contents of imem (hex, n*v repeats v):
  //   6300013 500093 ffd00113 4208a63 4109863 420c663 410c463 4115263 100a13 10d463 30900f13 a93 300b13
  //   16a8ab3 fffb0b13 fe0b1ce3 2200d13 1a09db3 1a15e33 10aeb3 c00bef 2a00c13 c0006f b8ce7 37800f13 6f
  //   IMEM
  //   DECODE/REGESTER READ
  //   CONTROL
  //   EXECUTE
  //   Current PC and Data values
  //   Control values
  //   halt is 1 when the program enters an infinite loop instruction.
  //   (And all the example programs end with the infinite loop instruction)
  //   MEMORY ACCESS
  //   DMEM
  //   REGESTER WRITE
endmodule

module regfile (
  input  [31:0] input_data,
  input  [4:0] address_rd,
  input  [4:0] address_rs1,
  input  [4:0] address_rs2,
  input  write_enable,
  input  clk,
  input  reset,
  output [31:0] data_rs1,
  output [31:0] data_rs2
);

  wire write_enable_0, write_enable_1, write_enable_2, write_enable_3, write_enable_4, write_enable_5,
       write_enable_6, write_enable_7, write_enable_8, write_enable_9, write_enable_10, write_enable_11,
       write_enable_12, write_enable_13, write_enable_14, write_enable_15, write_enable_16, write_enable_17,
       write_enable_18, write_enable_19, write_enable_20, write_enable_21, write_enable_22, write_enable_23,
       write_enable_24, write_enable_25, write_enable_26, write_enable_27, write_enable_28, write_enable_29,
       write_enable_30, write_enable_31;
  wire [31:0] output_1, output_2, output_3, output_4, output_5, output_6, output_7, output_8, output_9,
       output_10, output_11, output_12, output_13, output_14, output_15, output_16, output_17, output_18,
       output_19, output_20, output_21, output_22, output_23, output_24, output_25, output_26, output_27,
       output_28, output_29, output_30, output_31;

  Decoder #(.select(5)) decoder_1 (
    .out0(write_enable_0), .out1(write_enable_1), .out2(write_enable_2), .out3(write_enable_3),
    .out4(write_enable_4), .out5(write_enable_5), .out6(write_enable_6), .out7(write_enable_7),
    .out8(write_enable_8), .out9(write_enable_9), .out10(write_enable_10), .out11(write_enable_11),
    .out12(write_enable_12), .out13(write_enable_13), .out14(write_enable_14), .out15(write_enable_15),
    .out16(write_enable_16), .out17(write_enable_17), .out18(write_enable_18), .out19(write_enable_19),
    .out20(write_enable_20), .out21(write_enable_21), .out22(write_enable_22), .out23(write_enable_23),
    .out24(write_enable_24), .out25(write_enable_25), .out26(write_enable_26), .out27(write_enable_27),
    .out28(write_enable_28), .out29(write_enable_29), .out30(write_enable_30), .out31(write_enable_31),
    .sel(address_rd), .en(write_enable));
  Register #(.width(32)) x1 (.D(input_data), .en(write_enable_1), .clk(clk), .Q(output_1), .clr(reset));
  Register #(.width(32)) x2 (.D(input_data), .en(write_enable_2), .clk(clk), .Q(output_2), .clr(reset));
  Register #(.width(32)) x3 (.D(input_data), .en(write_enable_3), .clk(clk), .Q(output_3), .clr(reset));
  Register #(.width(32)) x4 (.D(input_data), .en(write_enable_4), .clk(clk), .Q(output_4), .clr(reset));
  Register #(.width(32)) x5 (.D(input_data), .en(write_enable_5), .clk(clk), .Q(output_5), .clr(reset));
  Register #(.width(32)) x6 (.D(input_data), .en(write_enable_6), .clk(clk), .Q(output_6), .clr(reset));
  Register #(.width(32)) x7 (.D(input_data), .en(write_enable_7), .clk(clk), .Q(output_7), .clr(reset));
  Register #(.width(32)) x8 (.D(input_data), .en(write_enable_8), .clk(clk), .Q(output_8), .clr(reset));
  Register #(.width(32)) x9 (.D(input_data), .en(write_enable_9), .clk(clk), .Q(output_9), .clr(reset));
  Register #(.width(32)) x10 (.D(input_data), .en(write_enable_10), .clk(clk), .Q(output_10), .clr(reset));
  Register #(.width(32)) x11 (.D(input_data), .en(write_enable_11), .clk(clk), .Q(output_11), .clr(reset));
  Register #(.width(32)) x12 (.D(input_data), .en(write_enable_12), .clk(clk), .Q(output_12), .clr(reset));
  Register #(.width(32)) x13 (.D(input_data), .en(write_enable_13), .clk(clk), .Q(output_13), .clr(reset));
  Register #(.width(32)) x14 (.D(input_data), .en(write_enable_14), .clk(clk), .Q(output_14), .clr(reset));
  Register #(.width(32)) x15 (.D(input_data), .en(write_enable_15), .clk(clk), .Q(output_15), .clr(reset));
  Register #(.width(32)) x16 (.D(input_data), .en(write_enable_16), .clk(clk), .Q(output_16), .clr(reset));
  Register #(.width(32)) x17 (.D(input_data), .en(write_enable_17), .clk(clk), .Q(output_17), .clr(reset));
  Register #(.width(32)) x18 (.D(input_data), .en(write_enable_18), .clk(clk), .Q(output_18), .clr(reset));
  Register #(.width(32)) x19 (.D(input_data), .en(write_enable_19), .clk(clk), .Q(output_19), .clr(reset));
  Register #(.width(32)) x20 (.D(input_data), .en(write_enable_20), .clk(clk), .Q(output_20), .clr(reset));
  Register #(.width(32)) x21 (.D(input_data), .en(write_enable_21), .clk(clk), .Q(output_21), .clr(reset));
  Register #(.width(32)) x22 (.D(input_data), .en(write_enable_22), .clk(clk), .Q(output_22), .clr(reset));
  Register #(.width(32)) x23 (.D(input_data), .en(write_enable_23), .clk(clk), .Q(output_23), .clr(reset));
  Register #(.width(32)) x24 (.D(input_data), .en(write_enable_24), .clk(clk), .Q(output_24), .clr(reset));
  Register #(.width(32)) x25 (.D(input_data), .en(write_enable_25), .clk(clk), .Q(output_25), .clr(reset));
  Register #(.width(32)) x26 (.D(input_data), .en(write_enable_26), .clk(clk), .Q(output_26), .clr(reset));
  Register #(.width(32)) x27 (.D(input_data), .en(write_enable_27), .clk(clk), .Q(output_27), .clr(reset));
  Register #(.width(32)) x28 (.D(input_data), .en(write_enable_28), .clk(clk), .Q(output_28), .clr(reset));
  Register #(.width(32)) x29 (.D(input_data), .en(write_enable_29), .clk(clk), .Q(output_29), .clr(reset));
  Register #(.width(32)) x30 (.D(input_data), .en(write_enable_30), .clk(clk), .Q(output_30), .clr(reset));
  Register #(.width(32)) x31 (.D(input_data), .en(write_enable_31), .clk(clk), .Q(output_31), .clr(reset));
  Multiplexer #(.select(5), .width(32)) multiplexer_1 (
    .in0({32{1'b0}}), .in1(output_1), .in2(output_2), .in3(output_3), .in4(output_4), .in5(output_5),
    .in6(output_6), .in7(output_7), .in8(output_8), .in9(output_9), .in10(output_10), .in11(output_11),
    .in12(output_12), .in13(output_13), .in14(output_14), .in15(output_15), .in16(output_16),
    .in17(output_17), .in18(output_18), .in19(output_19), .in20(output_20), .in21(output_21),
    .in22(output_22), .in23(output_23), .in24(output_24), .in25(output_25), .in26(output_26),
    .in27(output_27), .in28(output_28), .in29(output_29), .in30(output_30), .in31(output_31), .out(data_rs1),
    .sel(address_rs1));
  Multiplexer #(.select(5), .width(32)) multiplexer_2 (
    .in0({32{1'b0}}), .in1(output_1), .in2(output_2), .in3(output_3), .in4(output_4), .in5(output_5),
    .in6(output_6), .in7(output_7), .in8(output_8), .in9(output_9), .in10(output_10), .in11(output_11),
    .in12(output_12), .in13(output_13), .in14(output_14), .in15(output_15), .in16(output_16),
    .in17(output_17), .in18(output_18), .in19(output_19), .in20(output_20), .in21(output_21),
    .in22(output_22), .in23(output_23), .in24(output_24), .in25(output_25), .in26(output_26),
    .in27(output_27), .in28(output_28), .in29(output_29), .in30(output_30), .in31(output_31), .out(data_rs2),
    .sel(address_rs2));

  // Other names for the same wires on the sheet: input[31:0] = input_data

  // Notes on the sheet:
  //   address_rs1: initial=0x5
  //   address_rs2: initial=0x6
  //   X0
endmodule

module alu (
  input  [31:0] rs1,
  input  [31:0] rs2,
  input  [3:0] alu_select,
  output [31:0] rd
);

  wire comparator_1_lt;
  wire [31:0] adder_1_out, and_1_out, bit_extender_1_out, multiplier_1_out, or_1_out, shifter_1_out,
       shifter_2_out, subtractor_1_out, xor_1_out;

  Adder #(.width(32)) adder_1 (.a(rs1), .b(rs2), .out(adder_1_out));  // open: cin, cout
  Subtractor #(.width(32)) subtractor_1 (.a(rs1), .b(rs2), .out(subtractor_1_out));  // open: bin, bout
  Shifter #(.width(32)) shifter_1 (.in(rs1), .\dist (rs2[4:0]), .out(shifter_1_out));
  Shifter #(.shift("lr"), .width(32)) shifter_2 (.in(rs1), .\dist (rs2[4:0]), .out(shifter_2_out));
  Comparator #(.width(32)) comparator_1 (.a(rs1), .b(rs2), .lt(comparator_1_lt));  // open: gt, eq
  Multiplier #(.width(32)) multiplier_1 (.a(rs1), .b(rs2), .out(multiplier_1_out));  // open: cin, cout
  assign and_1_out = rs1 & rs2;  // AND_Gate and_1, 32 bits wide
  assign or_1_out = rs1 | rs2;  // OR_Gate or_1, 32 bits wide
  assign xor_1_out = rs1 ^ rs2;  // XOR_Gate xor_1, 32 bits wide
  assign bit_extender_1_out = {{31{1'b0}}, comparator_1_lt};  // Bit_Extender bit_extender_1
  Multiplexer #(.select(4), .width(32)) multiplexer_1 (
    .in0(adder_1_out), .in1(subtractor_1_out), .in2(and_1_out), .in3(or_1_out), .in4(xor_1_out),
    .in5(shifter_1_out), .in6(shifter_2_out), .in7(bit_extender_1_out), .in8(multiplier_1_out), .in9(rs2),
    .out(rd), .sel(alu_select));  // open: in10, in11, in12, in13, in14, in15

  // Other names for the same wires on the sheet: B[31:0] = rs2
endmodule

module better_control (
  input  [31:0] instruction,
  input  eq,
  input  lt,
  output [3:0] alu_select,
  output get_immediate,
  output enable_rd_write,
  output [2:0] Imm_type,
  output jump,
  output [1:0] select_rd_write,
  output next_pc_select,
  output dmem_write_enable
);

  wire add, alu_and, alu_lui, alu_or, alu_out, alu_sll, alu_slt, alu_sltu, alu_sra, alu_srl, alu_xor,
       and_12_out, and_13_out, and_14_out, and_16_out, and_17_out, and_18_out, and_19_out, and_20_out,
       and_21_out, and_30_out, and_31_out, and_32_out, and_33_out, and_35_out, and_36_out,
       B_type_branch_instr, branch_true, dmem, f3_000, f3_001, f3_010, f3_011, f3_100, f3_101, f3_110,
       f3_111, f7_0000000, f7_0000001, f7_0100000, force_alu_add, I_type_arithmetic_instr, I_type_instr,
       I_type_jalr_instr, I_type_load_instr, J_type_jal_instr, mul, or_2_out, or_3_out, or_7_out, or_9_out,
       PCplus4, R_type_instr, sub;
  wire [3:0] priority_encoder_1_out;

  Decoder #(.select(3)) decoder_1 (
    .out0(f3_000), .out1(f3_001), .out2(f3_010), .out3(f3_011), .out4(f3_100), .out5(f3_101), .out6(f3_110),
    .out7(f3_111), .sel(instruction[14:12]));  // open: en
  and and_1 (f7_0000000, ~instruction[25], ~instruction[26], ~instruction[27], ~instruction[28], ~instruction[29], ~instruction[30], ~instruction[31]);  // AND_Gate
  and and_2 (f7_0100000, ~instruction[25], ~instruction[26], ~instruction[27], ~instruction[28], ~instruction[29], instruction[30], ~instruction[31]);  // AND_Gate
  and and_3 (f7_0000001, instruction[25], ~instruction[26], ~instruction[27], ~instruction[28], ~instruction[29], ~instruction[30], ~instruction[31]);  // AND_Gate
  and and_4 (R_type_instr, instruction[0], instruction[1], ~instruction[2], ~instruction[3], instruction[4], instruction[5], ~instruction[6]);  // AND_Gate
  and and_5 (I_type_arithmetic_instr, instruction[0], instruction[1], ~instruction[2], ~instruction[3], instruction[4], ~instruction[5], ~instruction[6]);  // AND_Gate
  and and_6 (I_type_load_instr, instruction[0], instruction[1], ~instruction[2], ~instruction[3], ~instruction[4], ~instruction[5], ~instruction[6]);  // AND_Gate
  and and_7 (dmem_write_enable, instruction[0], instruction[1], ~instruction[2], ~instruction[3], ~instruction[4], instruction[5], ~instruction[6]);  // AND_Gate
  and and_8 (B_type_branch_instr, instruction[0], instruction[1], ~instruction[2], ~instruction[3], ~instruction[4], instruction[5], instruction[6]);  // AND_Gate
  and and_9 (alu_lui, instruction[0], instruction[1], instruction[2], ~instruction[3], instruction[4], instruction[5], ~instruction[6]);  // AND_Gate
  and and_10 (J_type_jal_instr, instruction[0], instruction[1], instruction[2], instruction[3], ~instruction[4], instruction[5], instruction[6]);  // AND_Gate
  and and_11 (I_type_jalr_instr, instruction[0], instruction[1], instruction[2], ~instruction[3], ~instruction[4], instruction[5], instruction[6]);  // AND_Gate
  and and_12 (and_12_out, dmem_write_enable, f3_010);
  and and_13 (and_13_out, I_type_load_instr, f3_010);
  and and_14 (and_14_out, I_type_jalr_instr, f3_000);
  and and_15 (sub, R_type_instr, f3_000, f7_0100000);
  and and_16 (and_16_out, R_type_instr, f3_110, f7_0000000);
  and and_17 (and_17_out, I_type_arithmetic_instr, f3_110);
  and and_18 (and_18_out, R_type_instr, f3_100, f7_0000000);
  and and_19 (and_19_out, I_type_arithmetic_instr, f3_100);
  or or_1 (force_alu_add, and_13_out, and_12_out, B_type_branch_instr, J_type_jal_instr, and_14_out);
  and and_20 (and_20_out, R_type_instr, f7_0000000);
  or or_2 (or_2_out, and_20_out, I_type_arithmetic_instr);
  and and_21 (and_21_out, R_type_instr, f7_0000000);
  and and_22 (alu_sll, R_type_instr, f3_001, f7_0000000);
  and and_23 (alu_srl, R_type_instr, f3_101, f7_0000000);
  and and_24 (alu_slt, R_type_instr, f3_010, f7_0000000);
  and and_25 (mul, R_type_instr, f3_000, f7_0000001);
  and and_26 (alu_sra, R_type_instr, f3_101, f7_0100000);
  and and_27 (alu_sltu, R_type_instr, f3_011, f7_0000000);
  and and_28 (add, or_2_out, f3_000);
  or or_3 (or_3_out, and_21_out, I_type_arithmetic_instr);
  and and_29 (alu_and, or_3_out, f3_111);
  or or_4 (alu_or, and_16_out, and_17_out);
  or or_5 (alu_xor, and_18_out, and_19_out);
  or or_6 (I_type_instr, I_type_arithmetic_instr, I_type_load_instr, I_type_jalr_instr);
  not not_1 (get_immediate, R_type_instr);
  Priority_Encoder #(.disabled("Z"), .select(4)) priority_encoder_1 (
    .in0(add), .in1(sub), .in2(alu_and), .in3(alu_or), .in4(alu_xor), .in5(alu_sll), .in6(alu_srl),
    .in7(alu_slt), .in8(mul), .in9(alu_lui), .out(priority_encoder_1_out), .en_in(or_7_out));  // open: in10, in11, in12, in13, in14, in15, gs, en_out
  or or_7 (or_7_out, R_type_instr, I_type_arithmetic_instr, B_type_branch_instr, alu_lui, force_alu_add);
  and and_30 (and_30_out, eq, f3_000);
  and and_31 (and_31_out, ~eq, f3_001);  // AND_Gate
  and and_32 (and_32_out, lt, f3_100);
  and and_33 (and_33_out, ~lt, f3_101);  // AND_Gate
  or or_8 (alu_out, add, sub, alu_and, alu_or, alu_xor, alu_sll, alu_srl, alu_slt, mul, alu_lui);
  Multiplexer #(.width(4)) multiplexer_1 (
    .in0(priority_encoder_1_out), .in1(4'b0000), .out(alu_select), .sel(force_alu_add));
  or or_9 (or_9_out, and_30_out, and_31_out, and_32_out, and_33_out);
  and and_34 (dmem, I_type_load_instr, f3_010);
  or or_10 (enable_rd_write, R_type_instr, I_type_instr, alu_lui, J_type_jal_instr);
  and and_35 (and_35_out, I_type_jalr_instr, f3_000);
  and and_36 (and_36_out, I_type_jalr_instr, f3_000);
  Priority_Encoder priority_encoder_2 (
    .in0(I_type_instr), .in1(dmem_write_enable), .in2(B_type_branch_instr), .in3(alu_lui),
    .in4(J_type_jal_instr), .out(Imm_type));  // open: in5, in6, in7, en_in, gs, en_out
  and and_37 (branch_true, or_9_out, B_type_branch_instr);
  or or_11 (PCplus4, J_type_jal_instr, and_35_out);
  or or_12 (next_pc_select, J_type_jal_instr, branch_true, and_36_out);
  Priority_Encoder #(.disabled("Z"), .select(2)) priority_encoder_3 (
    .in0(dmem), .in1(alu_out), .in2(PCplus4), .out(select_rd_write));  // open: in3, gs, en_out, en_in
  or or_13 (jump, branch_true, J_type_jal_instr);

  // Other names for the same wires on the sheet: U_type_lui_instr = alu_lui; opcode[6:0] = instruction[6:0];
  //   func3[2:0] = instruction[14:12]; func7[6:0] = instruction[31:25]; S_type_store_instr = dmem_write_enable

  // Notes on the sheet:
  //   instruction: initial=0x510167
endmodule

module get_immediate_value (
  input  [31:0] instruction,
  input  [2:0] Imm_type,
  output [31:0] Immediate
);

  wire [31:0] b_type, I_type, j_type, s_type;

  assign I_type = {{20{instruction[31]}}, instruction[31:20]};  // Bit_Extender bit_extender_1
  assign s_type = {{20{instruction[31]}}, {instruction[31:25], instruction[11:7]}};  // Bit_Extender bit_extender_2
  assign b_type = {{19{instruction[31]}}, {instruction[31], instruction[7], instruction[30:25], instruction[11:8], 1'b0}};  // Bit_Extender bit_extender_3
  assign j_type = {{11{instruction[31]}}, {instruction[31], instruction[19:12], instruction[20], instruction[30:21], 1'b0}};  // Bit_Extender bit_extender_4
  Multiplexer #(.select(3), .width(32)) multiplexer_1 (
    .in0(I_type), .in1(s_type), .in2(b_type), .in3({instruction[31:12], {12{1'b0}}}), .in4(j_type),
    .out(Immediate), .sel(Imm_type));  // open: in5, in6, in7

  // Other names for the same wires on the sheet: U_type[31:12] = instruction[31:12]

  // Notes on the sheet:
  //   ADDRESS_RD
  //   address_rs1
  //   i_type_imm[11:0]
  //   instr[7:11]=imm[0:4]
  //   instr[25:31]=imm[5:11]
  //   instr[7]=imm[11]
  //   instr[8:11]=imm[1:4]
  //   instr[25:30]=imm[5:10]
  //   instr[31]=imm[12]
  //   instr[12:31]=imm[12:31]
  //   0=imm[0]
  //   instr[12:19]=imm[12:19]
  //   instr[20]=imm[11]
  //   instr[21:30]=imm[1:10]
  //   instr[31]=imm[20]
  //   0=imm[0]
  //   0[0:11]=imm[0:11]
endmodule

module test_run (
  input  reset,
  output [31:0] current_pc,
  output [31:0] current_instruction,
  output [31:0] alu_output,
  output [31:0] dmem_output,
  output [31:0] rd_write_value,
  output [31:0] data_rs1,
  output [31:0] data_rs2,
  output [31:0] imm_32bit,
  output halt,
  output [3:0] alu_select,
  output imm_vs_rs2_select,
  output enable_rd_write,
  output [2:0] imm_type,
  output jump_or_branch,
  output [1:0] rd_write_select,
  output next_pc_select,
  output dmem_write_enable
);

  main main_1 (
    .reset(reset), .current_pc(current_pc), .current_instruction(current_instruction),
    .alu_output(alu_output), .dmem_output(dmem_output), .rd_write_value(rd_write_value), .data_rs1(data_rs1),
    .data_rs2(data_rs2), .imm_32bit(imm_32bit), .alu_select(alu_select),
    .imm_vs_rs2_select(imm_vs_rs2_select), .enable_rd_write(enable_rd_write), .imm_type(imm_type),
    .jump_branch(jump_or_branch), .rd_write_select(rd_write_select), .next_pc_select(next_pc_select),
    .dmem_write_enable(dmem_write_enable), .halt(halt));

  // Notes on the sheet:
  //   Control values
  //   PC and Data values
endmodule
